# Fritzing sketch Robot (saved by Fritzing 0.9.3b)
breadboards: 1

parts:
  Part1 = BluePill
  Part2 = SRF05 Ultrasonic Rangefinder
  S1 = H-Bridge with L298N
  M1 = Getriebemotor
  M2 = Getriebemotor
  M3 = Getriebemotor
  M4 = Getriebemotor
  VCC1 = Battery block 9V
  J1 = Basic Servo

nets:
  N1: Part1.A0, S1.ENB
  N2: Part1.A1, S1.ENA
  N3: Part1.A3, S1.IN1
  N4: Part1.A4, S1.IN2
  N5: Part1.A5, S1.IN3
  N6: Part1.A6, S1.IN4
  GND: Part1.GND, S1.GND, VCC1.-
  GND_2: Part1.GND2, Part2.GND, J1.gnd
  5V: Part1.5V, Part2.VCC, S1.5V, J1.vcc
  N7: Part1.A9, Part2.Trig
  N8: Part1.A8, Part2.Echo
  N9: S1.12V, VCC1.+
  N10: S1.M1-01, M4.pin_1
  N11: S1.M1-02, M1.pin_1, M4.pin_2
  N12: S1.M2-01, M2.pin_1
  N13: S1.M2-02, M2.pin_2, M3.pin_1

custom parts:
  H-Bridge with L298N: h-bridge
